# Fritzing sketch BLE4-Schematics (saved by Fritzing 0.9.2b)

parts:
  Part1 = Bluetooth HM-10
  Part2 = Arduino Pro Mini v13
  USB1 = Wiring USB Adapter

nets:
  N1: Part1.RXD, Part2.D11_PWM/MOSI
  N2: Part1.TXD, Part2.D10_PWM/SS
  GND: Part1.GND, Part2.GND, USB1.GND
  VCC: Part1.VCC, Part2.VCC, USB1.5V
  N3: Part2.D0/TX, USB1.RX
  N4: Part2.D1/RX, USB1.TX

notes:
  Arduino Pro Mini
  ATmega328 (3.3V, 8 MHz)
